// Logisim project thebestsofar.circ as structural Verilog: 11 circuits, main circuit tensjk
module timemode (
  output [1:0] out_1
);

  wire aaalarm, alarmd, alarmddd, am, and_1_out, and_2_out, and_3_out, bcd_to_7_segment_decoder_5_p2,
       clock_1_out, clock_2_out, clock_3_out, comparator_1_eq, comparator_2_eq, comparator_3_eq,
       comparator_4_eq, demultiplexer_2_out0, demultiplexer_2_out1, demultiplexer_2_out2, hhourset, hourset,
       hoursetalrm, hoursettimer, minuteset, minutesetalrm, minutesettimer, mminuteset, moddes,
       multiplexer_7_out, multiplexer_8_out, multiplexer_12_out, multiplexer_13_out, or_1_out, pm, resetalrm,
       resetsw, resettt, resettter, rreset, set, setactive, setalrm, settimer, sset, sstart, startsw,
       starttimer, stopalarm, t_ff_1_q, t_ff_5_q, the24converter, the_0_to_60jk_1_out_5,
       the_0_to_60jk_2_out_5, the_0_to_60jk_3_out_5, the_0_to_60jk_4_out_5, the_0_to_60jk_5_out_5,
       the_0_to_60jk_6_out_5, undriven;
  wire [3:0] comparatorfor1224_1_org0to2, comparatorfor1224_1_org0to9, comparatorfor1224_1_tensvl,
       comparatorfor1224_1_unitsvl, hourtens, hourunits, hr2, hr2alrm, hr2sw, hr2timer, hr9or4, hr9or4alrm,
       hr9or4sw, hr9or4timer, min5, min5alrm, min5sw, min5timer, min9, min9alrm, min9sw, min9timer, mintens,
       minunits, sec5, sec5alrm, sec5timer, sec6sw, sec9, sec9alrm, sec9sw, sec9timer, sectens, secunits,
       thehrtens, thehrunits;

  Demultiplexer #(.select(2)) demultiplexer_1 (
    .out0(hourset), .out1(hoursetalrm), .out2(hoursettimer), .in(hhourset), .sel(out_1));  // open: out3
  Multiplexer #(.select(2), .width(4)) multiplexer_1 (
    .in0(thehrtens), .in1(hr2alrm), .in2(hr2timer), .in3(hr2sw), .out(hourtens), .sel(out_1));
  unitsjk unitsjk_1 (.CLK(moddes), .out_3(out_1));  // open: CLR
  Multiplexer #(.select(2), .width(4)) multiplexer_2 (
    .in0(thehrunits), .in1(hr9or4alrm), .in2(hr9or4timer), .in3(hr9or4sw), .out(hourunits), .sel(out_1));
  Multiplexer #(.select(2), .width(4)) multiplexer_3 (
    .in0(min5), .in1(min5alrm), .in2(min5timer), .in3(min5sw), .out(mintens), .sel(out_1));
  Multiplexer #(.select(2), .width(4)) multiplexer_4 (
    .in0(min9), .in1(min9alrm), .in2(min9timer), .in3(min9sw), .out(minunits), .sel(out_1));
  Multiplexer #(.select(2), .width(4)) multiplexer_5 (
    .in0(sec5), .in1(sec5alrm), .in2(sec5timer), .in3(sec6sw), .out(sectens), .sel(out_1));
  Multiplexer #(.select(2), .width(4)) multiplexer_6 (
    .in0(sec9), .in1(sec9alrm), .in2(sec9timer), .in3(sec9sw), .out(secunits), .sel(out_1));
  Clock clock_1 (.out(clock_1_out));
  Demultiplexer #(.select(2)) demultiplexer_2 (
    .out0(demultiplexer_2_out0), .out1(demultiplexer_2_out1), .out2(demultiplexer_2_out2), .in(sset),
    .sel(out_1));  // open: out3
  T_Flip_Flop t_ff_1 (.T(1'b1), .clk(startsw), .Q(t_ff_1_q));  // open: Qn, reset, preset
  Clock clock_2 (.out(clock_2_out));
  T_Flip_Flop t_ff_2 (.T(1'b1), .clk(demultiplexer_2_out0), .Q(set));  // open: Qn, reset, preset
  T_Flip_Flop t_ff_3 (.T(1'b1), .clk(demultiplexer_2_out1), .Q(setalrm));  // open: Qn, reset, preset
  T_Flip_Flop t_ff_4 (.T(1'b1), .clk(demultiplexer_2_out2), .Q(settimer));  // open: Qn, reset, preset
  the_0_to_60jk the_0_to_60jk_1 (
    .in_1(clock_1_out), .in_2(resettt), .to9(sec5), .to5(sec9), .out_5(the_0_to_60jk_1_out_5));
  and and_1 (and_1_out, t_ff_1_q, clock_2_out);
  _7_Segment_Display u_7_segment_display_1 ();  // open: g, f, a, b, e, d, c, dp
  // BCD_to_7_Segment_decoder bcd_to_7_segment_decoder_1: pin names not known; wires that end beside it: hourtens
  the_0_to_60jk the_0_to_60jk_2 (
    .in_2(resetalrm), .to9(sec5alrm), .to5(sec9alrm), .out_5(the_0_to_60jk_2_out_5));  // open: in_1
  comparatorfor1224 comparatorfor1224_1 (
    .for2and1(hr2), .for0to9h(hr9or4), .org0to2(comparatorfor1224_1_org0to2), .am(am), .pm(pm),
    .tensvl(comparatorfor1224_1_tensvl), .org0to9(comparatorfor1224_1_org0to9),
    .unitsvl(comparatorfor1224_1_unitsvl));
  Multiplexer multiplexer_7 (.in0(the_0_to_60jk_1_out_5), .in1(minuteset), .out(multiplexer_7_out), .sel(set));
  _7_Segment_Display u_7_segment_display_2 ();  // open: g, f, a, b, e, d, c, dp
  // BCD_to_7_Segment_decoder bcd_to_7_segment_decoder_2: pin names not known; wires that end beside it: hourunits
  Multiplexer multiplexer_8 (.in0(the_0_to_60jk_2_out_5), .in1(minutesetalrm), .out(multiplexer_8_out), .sel(setalrm));
  Multiplexer #(.width(4)) multiplexer_9 (
    .in0(comparatorfor1224_1_org0to2), .in1(comparatorfor1224_1_tensvl), .out(thehrtens), .sel(t_ff_5_q));
  Multiplexer #(.width(4)) multiplexer_10 (
    .in0(comparatorfor1224_1_org0to9), .in1(comparatorfor1224_1_unitsvl), .out(thehrunits), .sel(t_ff_5_q));
  Multiplexer #(.select(2)) multiplexer_11 (
    .in0(set), .in1(setalrm), .in2(settimer), .out(setactive), .sel(out_1));  // open: in3
  _7_Segment_Display u_7_segment_display_3 ();  // open: g, f, a, b, e, d, c, dp
  // BCD_to_7_Segment_decoder bcd_to_7_segment_decoder_3: pin names not known; wires that end beside it: minunits
  the_0_to_60jk the_0_to_60jk_3 (
    .in_1(and_1_out), .in_2(resetsw), .to9(sec6sw), .to5(sec9sw), .out_5(the_0_to_60jk_3_out_5));
  T_Flip_Flop t_ff_5 (.T(1'b1), .clk(the24converter), .Q(t_ff_5_q));  // open: Qn, reset, preset
  _7_Segment_Display u_7_segment_display_4 ();  // open: g, f, a, b, e, d, c, dp
  // BCD_to_7_Segment_decoder bcd_to_7_segment_decoder_4: pin names not known; wires that end beside it: mintens
  the_0_to_60jk the_0_to_60jk_4 (
    .in_1(multiplexer_7_out), .in_2(resettt), .to9(min5), .to5(min9), .out_5(the_0_to_60jk_4_out_5));
  _7_Segment_Display u_7_segment_display_5 ();  // open: g, f, a, b, e, d, c, dp
  _7_Segment_Display u_7_segment_display_6 ();  // open: g, f, a, b, e, d, c, dp
  // BCD_to_7_Segment_decoder bcd_to_7_segment_decoder_5: pin names not known; wires that end beside it: sectens, bcd_to_7_segment_decoder_5_p2, bcd_to_7_segment_decoder_5_p2
  // BCD_to_7_Segment_decoder bcd_to_7_segment_decoder_6: pin names not known; wires that end beside it: secunits
  the_0_to_60jk the_0_to_60jk_5 (
    .in_1(multiplexer_8_out), .in_2(resetalrm), .to9(min5alrm), .to5(min9alrm), .out_5(the_0_to_60jk_5_out_5));
  Demultiplexer #(.select(2)) demultiplexer_3 (
    .out0(resettt), .out1(resetalrm), .out2(resettter), .out3(resetsw), .in(rreset), .sel(out_1));
  Multiplexer multiplexer_12 (.in0(the_0_to_60jk_4_out_5), .in1(hourset), .out(multiplexer_12_out), .sel(set));
  Clock clock_3 (.out(clock_3_out));
  LED led_1 (.in(am));
  LED led_2 (.in(pm));
  LED alarm (.in(aaalarm));
  LED led_3 (.in(setactive));
  Multiplexer multiplexer_13 (.in0(the_0_to_60jk_5_out_5), .in1(hoursetalrm), .out(multiplexer_13_out), .sel(setalrm));
  the_0_to_60jk the_0_to_60jk_6 (
    .in_1(the_0_to_60jk_3_out_5), .in_2(resetsw), .to9(min5sw), .to5(min9sw), .out_5(the_0_to_60jk_6_out_5));
  zero_to_24 zero_to_24_1 (.ADV(multiplexer_12_out), .CLR(resettt), .to_9or4(hr9or4), .to_2(hr2));  // open: CLK
  Button button_1 (.out(sstart));
  Button button_2 (.out(moddes));
  Button button_3 (.out(mminuteset));
  Button button_4 (.out(hhourset));
  ccccc ccccc_1 (
    .rreset(settimer), .sssett(resettter), .sstart(starttimer), .crok(clock_3_out), .minsets(minutesettimer),
    .hrset(hoursettimer), .alrmoff(undriven), .secdstens(hr2timer), .mintenss(hr9or4timer),
    .secdunits(min9timer), .minunitss(min5timer), .hrstensss(sec9timer), .hrsunitsss(sec5timer),
    .alarmmm(alarmd));
  Demultiplexer #(.select(2)) demultiplexer_4 (
    .out0(minuteset), .out1(minutesetalrm), .out2(minutesettimer), .in(mminuteset), .sel(out_1));  // open: out3
  zero_to_24 zero_to_24_2 (
    .ADV(multiplexer_13_out), .CLR(resetalrm), .to_9or4(hr9or4alrm), .to_2(hr2alrm));  // open: CLK
  Button button_5 (.out(sset));
  Button button_6 (.out(rreset));
  Button button_7 (.out(the24converter));
  Button button_8 (.out(stopalarm));
  zero_to_24 zero_to_24_3 (.ADV(the_0_to_60jk_6_out_5), .CLR(resetsw), .to_9or4(hr9or4sw), .to_2(hr2sw));  // open: CLK
  Demultiplexer #(.select(2)) demultiplexer_5 (
    .out2(starttimer), .out3(startsw), .in(sstart), .sel(out_1));  // open: out0, out1
  and and_2 (and_2_out, comparator_1_eq, comparator_4_eq);
  Comparator #(.mode("unsigned"), .width(4)) comparator_1 (
    .a(min5), .b(min5alrm), .eq(comparator_1_eq));  // open: gt, lt
  Comparator #(.mode("unsigned"), .width(4)) comparator_2 (
    .a(min9), .b(min9alrm), .eq(comparator_2_eq));  // open: gt, lt
  and and_3 (and_3_out, comparator_2_eq, comparator_3_eq);
  Comparator #(.mode("unsigned"), .width(4)) comparator_3 (.a(hr2), .b(hr2alrm), .eq(comparator_3_eq));  // open: gt, lt
  Comparator #(.mode("unsigned"), .width(4)) comparator_4 (
    .a(hr9or4), .b(hr9or4alrm), .eq(comparator_4_eq));  // open: gt, lt
  and and_4 (alarmddd, and_2_out, and_3_out);
  or or_1 (or_1_out, alarmddd, alarmd);
  T_Flip_Flop t_ff_6 (.T(1'b1), .clk(or_1_out), .Q(aaalarm), .reset(stopalarm));  // open: Qn, preset

  // Notes on the sheet:
  //   MODES
  //   Mode 00 is time
  //   Mode 01 is alarm
  //   Mode 10 is countdown
  //   Mode 11 is stopwatch
  //   THE 24HR TO 12HR FORMAT CONVERTER
  //   THE TIME KEEPING LOGIC
  //   THE ALARM LOGIC
  //   THE STOPWATCH
  //   THE COUNTDOWN TIMER 
  //   THE ALARM LOGIC
endmodule

module tensjk (
  input  CLK,
  input  CLR,
  output [3:0] out_3
);

  J_K_Flip_Flop #(.trigger("falling")) j_k_ff_1 (
    .J(1'b1), .K(1'b1), .clk(CLK), .Q(out_3[0]), .reset(CLR));  // open: Qn, preset
  J_K_Flip_Flop #(.trigger("falling")) j_k_ff_2 (
    .J(1'b1), .K(1'b1), .clk(out_3[0]), .Q(out_3[1]), .reset(CLR));  // open: Qn, preset
  J_K_Flip_Flop #(.trigger("falling")) j_k_ff_3 (
    .J(1'b1), .K(1'b1), .clk(out_3[1]), .Q(out_3[2]), .reset(CLR));  // open: Qn, preset
  J_K_Flip_Flop #(.trigger("falling")) j_k_ff_4 (
    .J(1'b1), .K(1'b1), .clk(out_3[2]), .Q(out_3[3]), .reset(CLR));  // open: Qn, preset
endmodule

module unitsjk (
  input  CLK,
  input  CLR,
  output [1:0] out_3
);

  J_K_Flip_Flop #(.trigger("falling")) j_k_ff_1 (
    .J(1'b1), .K(1'b1), .clk(CLK), .Q(out_3[0]), .reset(CLR));  // open: Qn, preset
  J_K_Flip_Flop #(.trigger("falling")) j_k_ff_2 (
    .J(1'b1), .K(1'b1), .clk(out_3[0]), .Q(out_3[1]), .reset(CLR));  // open: Qn, preset
endmodule

module the_0_to_60jk (
  input  in_1,
  input  in_2,
  output [3:0] to9,
  output [3:0] to5,
  output out_5
);

  wire and_1_out, not_1_out, not_2_out, or_1_out, or_2_out;

  or or_1 (or_1_out, in_2, and_1_out);
  tensjk tensjk_1 (.CLK(in_1), .CLR(or_1_out), .out_3(to9));
  not not_1 (not_1_out, to9[2]);
  and and_1 (and_1_out, to9[3], not_1_out, to9[1], ~to9[0]);  // AND_Gate
  or or_2 (or_2_out, in_2, out_5);
  tensjk tensjk_2 (.CLK(and_1_out), .CLR(or_2_out), .out_3(to5));
  not not_2 (not_2_out, to5[3]);
  and and_2 (out_5, not_2_out, to5[2], to5[1]);
endmodule

module for_7display (
  input  D,
  input  C,
  input  in_3,
  input  in_4,
  output a,
  output b,
  output out_7,
  output out_8,
  output e,
  output f,
  output g
);

  wire and_1_out, and_2_out, and_3_out, and_4_out, and_5_out, and_6_out, and_7_out, and_8_out, and_9_out,
       and_10_out, and_11_out, and_12_out, and_13_out, and_14_out, and_15_out, and_16_out, not_1_out,
       not_2_out, not_3_out;

  not not_1 (not_1_out, C);
  not not_2 (not_2_out, in_3);
  not not_3 (not_3_out, in_4);
  and and_1 (and_1_out, not_1_out, not_3_out);
  and and_2 (and_2_out, C, in_4);
  and and_3 (and_3_out, not_2_out, not_3_out);
  and and_4 (and_4_out, in_3, in_4);
  or or_1 (out_7, not_2_out, in_4, C);
  and and_5 (and_5_out, not_1_out, not_3_out);
  and and_6 (and_6_out, not_1_out, in_3);
  and and_7 (and_7_out, C, not_2_out, in_4);
  and and_8 (and_8_out, in_3, not_3_out);
  and and_9 (and_9_out, not_1_out, not_3_out);
  and and_10 (and_10_out, in_3, not_3_out);
  and and_11 (and_11_out, not_2_out, not_3_out);
  and and_12 (and_12_out, C, not_2_out);
  and and_13 (and_13_out, C, not_3_out);
  and and_14 (and_14_out, not_1_out, in_3);
  and and_15 (and_15_out, C, not_2_out);
  and and_16 (and_16_out, in_3, not_3_out);
  or or_2 (a, and_1_out, in_3, and_2_out, D);
  or or_3 (b, not_1_out, and_3_out, and_4_out);
  or or_4 (out_8, and_5_out, and_6_out, and_7_out, and_8_out, D);
  or or_5 (e, and_9_out, and_10_out);
  or or_6 (f, and_11_out, and_12_out, and_13_out, D);
  or or_7 (g, and_14_out, and_15_out, D, and_16_out);
endmodule

module zero_to_24 (
  input  ADV,
  input  CLK,
  input  CLR,
  output [3:0] to_9or4,
  output [3:0] to_2
);

  wire and_1_out, and_2_out, and_3_out, and_4_out, and_5_out, or_1_out, or_2_out, or_3_out, or_4_out;

  and and_1 (and_1_out, to_9or4[2], to_2[1]);
  and and_2 (and_2_out, to_2[1], ~CLK, to_2[0]);  // AND_Gate
  or or_1 (or_1_out, CLR, and_5_out);
  or or_2 (or_2_out, to_9or4[3], and_1_out);
  or or_3 (or_3_out, CLR, and_2_out);
  tensjk tensjk_1 (.CLK(ADV), .CLR(or_1_out), .out_3(to_9or4));
  tensjk tensjk_2 (.CLK(or_2_out), .CLR(or_3_out), .out_3(to_2));
  and and_3 (and_3_out, to_9or4[2], to_2[1]);
  and and_4 (and_4_out, ~to_2[1], to_9or4[1], to_9or4[3]);  // AND_Gate
  or or_4 (or_4_out, and_3_out, and_4_out);
  and and_5 (and_5_out, or_4_out, ~CLK);  // AND_Gate
endmodule

module bcd_to_binary (
  input  for1to2,
  input  in_2,
  input  in_3,
  input  in_4,
  input  for0to9,
  input  in_6,
  input  in_7,
  input  in_8,
  output [4:0] binary
);

  wire [4:0] multiplier_1_out;

  Multiplier #(.width(5)) multiplier_1 (
    .a({1'b0, in_4, in_3, in_2, for1to2}), .b(5'b01010), .out(multiplier_1_out));  // open: cin, cout
  Adder #(.width(5)) adder_1 (
    .a(multiplier_1_out), .b({1'b0, in_8, in_7, in_6, for0to9}), .out(binary));  // open: cin, cout
endmodule

module comparatorfor1224 (
  input  [3:0] for2and1,
  input  [3:0] for0to9h,
  output [3:0] org0to2,
  output am,
  output pm,
  output [3:0] tensvl,
  output [3:0] org0to9,
  output [3:0] unitsvl
);

  wire comparator_1_eq, comparator_2_gt, comparator_4_eq, comparator_5_lt, or_2_out;
  wire [1:0] comparator_3_eq;
  wire [4:0] adder_1_out, bcd_to_binary_1_binary, multiplexer_1_out, subtractor_1_out;

  bcd_to_binary bcd_to_binary_1 (
    .for1to2(for2and1[0]), .in_2(for2and1[1]), .in_3(for2and1[2]), .in_4(for2and1[3]), .for0to9(for0to9h[0]),
    .in_6(for0to9h[1]), .in_7(for0to9h[2]), .in_8(for0to9h[3]), .binary(bcd_to_binary_1_binary));
  Comparator #(.mode("unsigned"), .width(5)) comparator_1 (
    .a(bcd_to_binary_1_binary), .b(5'b01100), .eq(comparator_1_eq));  // open: gt, lt
  Comparator #(.mode("unsigned"), .width(5)) comparator_2 (
    .a(bcd_to_binary_1_binary), .b(5'b01100), .gt(comparator_2_gt));  // open: eq, lt
  Comparator #(.width(5)) comparator_3 (
    .a(bcd_to_binary_1_binary), .b({5{1'b0}}), .eq(comparator_3_eq[0]));  // open: gt, lt
  Comparator #(.mode("unsigned"), .width(5)) comparator_4 (
    .a(bcd_to_binary_1_binary), .b(5'b01100), .eq(comparator_4_eq));  // open: gt, lt
  Comparator #(.mode("unsigned"), .width(5)) comparator_5 (
    .a(bcd_to_binary_1_binary), .b(5'b01100), .lt(comparator_5_lt));  // open: gt, eq
  Comparator #(.mode("unsigned"), .width(5)) comparator_6 (
    .a(bcd_to_binary_1_binary), .b(5'b01100), .gt(comparator_3_eq[1]));  // open: eq, lt
  or or_1 (pm, comparator_1_eq, comparator_2_gt);
  or or_2 (or_2_out, comparator_4_eq, comparator_5_lt);
  Subtractor #(.width(5)) subtractor_1 (
    .a(bcd_to_binary_1_binary), .b(5'b01100), .out(subtractor_1_out));  // open: bin, bout
  not not_1 (am, pm);
  Adder #(.width(5)) adder_1 (.a(bcd_to_binary_1_binary), .b(5'b01100), .out(adder_1_out));  // open: cin, cout
  Multiplexer #(.select(2), .width(5)) multiplexer_1 (
    .in0(bcd_to_binary_1_binary), .in1(adder_1_out), .in2(subtractor_1_out), .out(multiplexer_1_out),
    .sel(comparator_3_eq));  // open: in3
  // Binary_to_BCD_converter #(.binvalue(5)) binary_to_bcd_converter_1: pin names not known; wires that end beside it: or_2_out, multiplexer_1_out, tensvl, unitsvl

  assign org0to2 = for2and1;
  assign org0to9 = for0to9h;
endmodule

module bcdtobinary (
  input  [5:0] for1to2,
  input  [5:0] for0to9,
  output [5:0] binary
);

  wire [5:0] multiplier_1_out;

  Multiplier #(.width(6)) multiplier_1 (.a(for1to2), .b(6'b001010), .out(multiplier_1_out));  // open: cin, cout
  Adder #(.width(6)) adder_1 (.a(multiplier_1_out), .b(for0to9), .out(binary));  // open: cin, cout
endmodule

module the4to6bit (
  input  [3:0] in_1,
  output [5:0] out_2
);


  assign out_2 = {2'b00, in_1};
endmodule

module ccccc (
  input  rreset,
  input  sssett,
  input  sstart,
  input  crok,
  input  minsets,
  input  hrset,
  input  alrmoff,
  output [3:0] secdstens,
  output [3:0] mintenss,
  output [3:0] secdunits,
  output [3:0] minunitss,
  output [3:0] hrstensss,
  output [3:0] hrsunitsss,
  output alarmmm
);

  wire and_1_out, and_2_out, and_3_out, comparator_1_eq, comparator_2_eq, comparator_3_eq, comparator_4_eq,
       comparator_5_eq, comparator_6_eq, counter_1_carry, counter_2_carry, demultiplexer_1_out1,
       demultiplexer_2_out1, demultiplexer_3_out1, multiplexer_1_out, multiplexer_2_out, multiplexer_3_out,
       multiplexer_4_out, multiplexer_5_out, multiplexer_6_out, not_1_out, or_1_out, or_2_out, or_3_out, set,
       t_ff_2_q;
  wire [5:0] binary_to_bcd_converter_1_p1, binary_to_bcd_converter_2_p1, binary_to_bcd_converter_3_p1;

  T_Flip_Flop t_ff_1 (.T(1'b1), .clk(sssett), .Q(set));  // open: Qn, reset, preset
  T_Flip_Flop t_ff_2 (.T(1'b1), .clk(sstart), .Q(t_ff_2_q));  // open: Qn, reset, preset
  T_Flip_Flop t_ff_3 (.T(1'b1), .clk(and_1_out), .Q(alarmmm));  // open: Qn, reset, preset
  and and_1 (and_1_out, not_1_out, and_3_out);
  not not_1 (not_1_out, alrmoff);
  Multiplexer multiplexer_1 (.in0(crok), .in1(1'b0), .out(multiplexer_1_out), .sel(alarmmm));
  and and_2 (and_2_out, t_ff_2_q, multiplexer_1_out);
  // Binary_to_BCD_converter #(.binvalue(6)) binary_to_bcd_converter_1: pin names not known; wires that end beside it: binary_to_bcd_converter_1_p1, secdstens, secdunits
  or or_1 (or_1_out, rreset, demultiplexer_1_out1);
  Counter #(.max('h3f), .trigger("falling"), .width(6)) counter_1 (
    .clr(or_1_out), .load(multiplexer_2_out), .up(set), .clk(and_2_out), .D(6'b111100),
    .carry(counter_1_carry), .Q(binary_to_bcd_converter_1_p1));  // open: count
  Multiplexer multiplexer_2 (.in0(comparator_2_eq), .in1(1'b0), .out(multiplexer_2_out), .sel(set));
  Demultiplexer demultiplexer_1 (.out1(demultiplexer_1_out1), .in(comparator_1_eq), .sel(set));  // open: out0
  // Binary_to_BCD_converter #(.binvalue(6)) binary_to_bcd_converter_2: pin names not known; wires that end beside it: binary_to_bcd_converter_2_p1, mintenss, minunitss
  Comparator #(.mode("unsigned"), .width(6)) comparator_1 (
    .a(binary_to_bcd_converter_1_p1), .b(6'b111100), .eq(comparator_1_eq));  // open: gt, lt
  Multiplexer multiplexer_3 (.in0(counter_1_carry), .in1(minsets), .out(multiplexer_3_out), .sel(set));
  Comparator #(.mode("unsigned"), .width(6)) comparator_2 (
    .a(binary_to_bcd_converter_1_p1), .b({6{1'b0}}), .eq(comparator_2_eq));  // open: gt, lt
  Multiplexer multiplexer_4 (.in0(comparator_4_eq), .in1(1'b0), .out(multiplexer_4_out), .sel(set));
  or or_2 (or_2_out, rreset, demultiplexer_2_out1);
  Counter #(.max('h3f), .trigger("falling"), .width(6)) counter_2 (
    .clr(or_2_out), .load(multiplexer_4_out), .up(set), .clk(multiplexer_3_out), .D(6'b111100),
    .carry(counter_2_carry), .Q(binary_to_bcd_converter_2_p1));  // open: count
  // Binary_to_BCD_converter #(.binvalue(6)) binary_to_bcd_converter_3: pin names not known; wires that end beside it: binary_to_bcd_converter_3_p1, hrstensss, hrsunitsss
  Demultiplexer demultiplexer_2 (.out1(demultiplexer_2_out1), .in(comparator_3_eq), .sel(set));  // open: out0
  and and_3 (and_3_out, comparator_2_eq, comparator_4_eq, comparator_6_eq);
  Comparator #(.mode("unsigned"), .width(6)) comparator_3 (
    .a(binary_to_bcd_converter_2_p1), .b(6'b111100), .eq(comparator_3_eq));  // open: gt, lt
  or or_3 (or_3_out, rreset, demultiplexer_3_out1);
  Multiplexer multiplexer_5 (.in0(counter_2_carry), .in1(hrset), .out(multiplexer_5_out), .sel(set));
  Comparator #(.mode("unsigned"), .width(6)) comparator_4 (
    .a(binary_to_bcd_converter_2_p1), .b({6{1'b0}}), .eq(comparator_4_eq));  // open: gt, lt
  Demultiplexer demultiplexer_3 (.out1(demultiplexer_3_out1), .in(comparator_5_eq), .sel(set));  // open: out0
  Multiplexer multiplexer_6 (.in0(comparator_6_eq), .in1(1'b0), .out(multiplexer_6_out), .sel(set));
  Counter #(.max('h3f), .trigger("falling"), .width(6)) counter_3 (
    .clr(or_3_out), .load(multiplexer_6_out), .up(set), .clk(multiplexer_5_out), .D(6'b111100),
    .Q(binary_to_bcd_converter_3_p1));  // open: count, carry
  Comparator #(.mode("unsigned"), .width(6)) comparator_5 (
    .a(binary_to_bcd_converter_3_p1), .b(6'b111100), .eq(comparator_5_eq));  // open: gt, lt
  Comparator #(.mode("unsigned"), .width(6)) comparator_6 (
    .a(binary_to_bcd_converter_3_p1), .b({6{1'b0}}), .eq(comparator_6_eq));  // open: gt, lt

  // Other names for the same wires on the sheet: reset = rreset
endmodule
